# Fritzing sketch Untitled Sketch (saved by Fritzing 0.9.3b)
breadboards: 1

parts:
  Composant1 = Arduino Uno (Rev3) - ICSP
  R1 = Resistor [tolerance=±5% resistance=220 package=THT]
  U1 = POT [package=trim_pot]
  RHT1 = Humidity and Temperature Sensor RHT03
  R2 = PHOTOCELL [package=photocell-kit]
  U2 = ESP8266 WiFi Module [part_number=ESP8266]

nets:
  N1: Composant1.A3, U1.A, R2.P$1
  5V: Composant1.5V, U1.S, RHT1.Vcc
  N2: Composant1.D9_PWM, R1.Pin_1, RHT1.Data-signal
  N3: Composant1.D10_PWM/SS, U2.RX
  N4: Composant1.D11_PWM/MOSI, U2.TX
  3V3: Composant1.3V3, U2.3.3V
  GND: Composant1.GND, RHT1.GND_2, R2.P$2, U2.GND
